# Fritzing sketch breadBoard (saved by Fritzing 0.9.2b)
circuit board: 8.46667cm x 5.64444cm
breadboards: 1

parts:
  LED1 = LED - 5mm [color="Red (633nm)" package="5 mm [THT]"]
  S1 = Pushbutton [package="[THT]"]
  R1 = Resistor [tolerance=±5% resistance=220 package=THT]
  S2 = Pushbutton [package="[THT]"]
  RHT1 = Humidity and Temperature Sensor RHT03
  to_sensor = Screw terminal - 2 pins [package=THT]
  to_power = Screw terminal - 2 pins [package=THT]
  LED2 = LED - 5mm [color="Red (633nm)" package="5 mm [THT]"]
  Part1 = Arduino Pro Mini v13

nets:
  N1: LED1.cathode, Part1.D2
  N2: LED1.anode, R1.Pin_1, S2.Pin_3, S2.Pin_4, RHT1.GND_2, to_power.pin1, LED2.anode, Part1.GND
  VCC: S1.Pin_1, S1.Pin_2, RHT1.Vcc, to_sensor.pin2, to_power.pin2, Part1.VCC
  N3: S1.Pin_3, S1.Pin_4, R1.Pin_0, to_sensor.pin1, Part1.D9_PWM
  N4: S2.Pin_1, S2.Pin_2, Part1.D8
  N5: RHT1.Data-signal, Part1.D12/MISO
  N6: LED2.cathode, Part1.D13/SCK
