# Fritzing sketch breadBoard2 (saved by Fritzing 0.9.2b)
breadboards: 1

parts:
  J1 = Piezo Speaker
  Arduino1 = Arduino Mini (Rev5)
  S1 = Pushbutton [package="[THT]"]
  S2 = Pushbutton [package="[THT]"]
  R1 = Resistor [tolerance=±5% resistance=220 package=THT]
  RHT1 = Humidity and Temperature Sensor RHT03
  LED1 = smd LED [color="Red (633nm)" package="1206 [SMD]"]

nets:
  N1: J1.pin1, Arduino1.GND, S2.Pin_1, S2.Pin_2, R1.Pin_1, RHT1.GND_2, LED1.anode
  N2: J1.pin2, Arduino1.D6_PWM
  N3: Arduino1.D2, LED1.cathode
  N4: Arduino1.D8, S2.Pin_3, S2.Pin_4
  5V: Arduino1.5V, RHT1.Vcc
  N5: Arduino1.D13, S1.Pin_3, S1.Pin_4, R1.Pin_0
  N6: Arduino1.D11_PWM, RHT1.Data-signal
  N7: S1.Pin_1, S1.Pin_2
